# Fritzing sketch DoubleADC (saved by Fritzing 0.9.4)

parts:
  Part2 = Adafruit ADS1015 12Bit I2C ADC [part_number="Adafruit #1083"]
  Part3 = Itsy Bitsy 32u4 5V @ 16MHz [part_number="Adafruit #3677"]
  Part4 = Adafruit ADS1015 12Bit I2C ADC [part_number="Adafruit #1083"]
  R1 = TRIMPOT [package=trimpot_pth_s3_lock]
  R2 = TRIMPOT [package=trimpot_pth_s3_lock]
  R3 = TRIMPOT [package=trimpot_pth_s3_lock]

nets:
  N1: Part2.AIN3, R2.WIPER
  N2: Part2.AIN1, R1.WIPER
  GND: Part2.ADDR, Part2.GND, Part3.GND, Part4.GND, R1.CCW, R2.CCW, R3.CCW
  N3: Part2.SDA, Part3.SDA, Part4.SDA
  N4: Part2.SCL, Part3.SCL, Part4.SCL
  VDD: Part2.VDD, Part3.+5V, Part4.ADDR, Part4.VDD, R1.CW, R2.CW, R3.CW
  N5: Part4.AIN1, R3.WIPER

custom parts:
  Adafruit ADS1015 12Bit I2C ADC: For microcontrollers without an analog-to-digital converter or when you want a higher-precision ADC, the ADS1015 provides 12-bit precision at 3300 samples/second over I2C. The chip can be configured as 4 single-ended input channels, or two differential channels. As a nice bonus, it even includes a programmable gain amplifier, up to x16, to help boost up smaller single/differential signals to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
  Itsy Bitsy 32u4 5V @ 16MHz: What's smaller than a Feather but larger than a Trinket? It's an Itsy Bitsy! Small, powerful, Arduino-compatible - this microcontroller board is perfect when you want something very compact, but still with a bunch of pins. Itsy Bitsy is only 1.4" long by 0.7" wide, but has 6 power pins, 6 analog & digital pins and 17 digital pins. It packs much of the same capability as an Arduino UNO. So it's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
